// Logisim project R10 A.circ as structural Verilog: 1 circuit, main circuit main
module main (
  input  A,
  input  B,
  input  C,
  output X,
  output Y
);

  wire and_1_out, or_1_out, xor_1_out;

  or or_1 (or_1_out, B, C);
  and and_1 (and_1_out, A, B);
  not not_1 (Y, or_1_out);
  xor xor_1 (xor_1_out, and_1_out, Y);
  not not_2 (X, xor_1_out);
endmodule
