// Logisim project StateMachine.circ as structural Verilog: 1 circuit, main circuit main
module main (
  input  In,
  output Out
);

  wire and_1_out, and_2_out, clock_1_out, or_1_out;

  and and_1 (and_1_out, Out, In);
  and and_2 (and_2_out, In, ~Out);  // AND_Gate
  or or_1 (or_1_out, and_1_out, and_2_out);
  Clock clock_1 (.out(clock_1_out));
  D_Flip_Flop d_ff_1 (.clk(clock_1_out), .D(or_1_out), .Q(Out));  // open: Qn, preset, en, reset

  // Notes on the sheet:
  //   A SIMPLE STATE MACHINE
  //   INPUT SECTION: Do not change anything here!
  //   You may only change the values of the inputs for testing using the hand tool.
  //   Do not introduce any other input or output pins in the circuit.
  //   To your logic
  //   OUTPUT SECTION: Do not change anything here!
  //   Do not introduce any other input or output pins in the circuit.
  //   From your logic
endmodule
